// Logisim project disabled1.circ as structural Verilog: 1 circuit, main circuit main
module main (
);

  wire Bit_1_q, Bit_1_qn, Clock_out;

  Clock Clock (.out(Clock_out));
  D_Flip_Flop Bit_1 (.clk(Clock_out), .D(Bit_1_qn), .Q(Bit_1_q), .Qn(Bit_1_qn));  // open: preset, en, reset
endmodule
