// Logisim project enabled.circ as structural Verilog: 1 circuit, main circuit main
module main (
);

  wire and_1_out, clock_1_out, d_ff_1_q, d_ff_1_qn, d_ff_2_qn;

  Clock clock_1 (.out(clock_1_out));
  D_Flip_Flop d_ff_1 (.clk(clock_1_out), .D(and_1_out), .Q(d_ff_1_q), .Qn(d_ff_1_qn));  // open: preset, en, reset
  D_Flip_Flop d_ff_2 (.clk(clock_1_out), .D(d_ff_1_q), .Qn(d_ff_2_qn));  // open: Q, preset, en, reset
  and and_1 (and_1_out, d_ff_1_qn, d_ff_2_qn);
endmodule
