// Logisim project semaforo.circ as structural Verilog: 1 circuit, main circuit main
module main (
);

  wire and_1_out, and_2_out, and_3_out, button_1_out, clock_1_out, d_ff_1_q, d_ff_1_qn, d_ff_2_q, d_ff_2_qn,
       nand_1_out;

  nand nand_1 (nand_1_out, button_1_out, d_ff_2_q);
  and and_1 (and_1_out, nand_1_out, d_ff_1_qn);
  LED led_1 (.in(and_2_out));
  and and_2 (and_2_out, d_ff_2_qn, button_1_out);
  D_Flip_Flop d_ff_1 (
    .clk(clock_1_out), .D(and_1_out), .Q(d_ff_1_q), .Qn(d_ff_1_qn), .preset(1'b0), .reset(1'b0));  // open: en
  LED led_2 (.in(d_ff_1_q));
  and and_3 (and_3_out, d_ff_2_q, button_1_out);
  LED led_3 (.in(and_3_out));
  D_Flip_Flop d_ff_2 (
    .clk(clock_1_out), .D(d_ff_1_q), .Q(d_ff_2_q), .Qn(d_ff_2_qn), .preset(1'b0), .reset(1'b0));  // open: en
  Clock clock_1 (.out(clock_1_out));
  Button button_1 (.out(button_1_out));
endmodule
