// Logisim project semaforo1.circ as structural Verilog: 1 circuit, main circuit main
module main (
);

  wire AND1_out, AND2_out, AND3_out, button_1_out, clock_1_out, d_ff_1_q, d_ff_1_qn, d_ff_2_q, d_ff_2_qn,
       NAND1_out;

  nand NAND1 (NAND1_out, button_1_out, d_ff_2_q);
  and AND1 (AND1_out, NAND1_out, d_ff_1_qn);
  LED led_1 (.in(AND2_out));
  and AND2 (AND2_out, d_ff_2_q, button_1_out);
  D_Flip_Flop d_ff_1 (
    .clk(clock_1_out), .D(AND1_out), .Q(d_ff_1_q), .Qn(d_ff_1_qn), .preset(1'b0), .reset(1'b0));  // open: en
  LED led_2 (.in(d_ff_1_q));
  and AND3 (AND3_out, d_ff_2_qn, button_1_out);
  LED led_3 (.in(AND3_out));
  D_Flip_Flop d_ff_2 (
    .clk(clock_1_out), .D(d_ff_1_q), .Q(d_ff_2_q), .Qn(d_ff_2_qn), .preset(1'b0), .reset(1'b0));  // open: en
  Clock clock_1 (.out(clock_1_out));
  Button button_1 (.out(button_1_out));

  // Notes on the sheet:
  //   Rosso
  //   Giallo
  //   Verde
endmodule
