// Logisim project solologica1.circ as structural Verilog: 1 circuit, main circuit main
module main (
  input  Enable
);

  wire And_1_out, Bit_1_q, Bit_1_qn, Bit_2_qn, Clock_out, Nand_1_out, undriven, undriven_2, undriven_3;

  Clock Clock (.out(Clock_out));
  D_Flip_Flop Bit_1 (
    .clk(Clock_out), .D(And_1_out), .Q(Bit_1_q), .Qn(Bit_1_qn), .preset(undriven), .en(undriven));  // open: reset
  D_Flip_Flop Bit_2 (
    .clk(Clock_out), .D(Bit_1_q), .Qn(Bit_2_qn), .preset(undriven_2), .en(undriven_2));  // open: Q, reset
  and And_1 (And_1_out, Bit_1_qn, Nand_1_out);
  nand Nand_1 (Nand_1_out, Bit_2_qn, undriven_3);

  // Notes on the sheet:
  //   EN: (NOT Q1) AND Q2
  //   EN: Q1
endmodule
